# Fritzing sketch DS18B20 (saved by Fritzing 0.7.7b)

parts:
  Arduino_Uno_and_Ethernet_shield = Arduino
  T1 = DS18B20 Temperature Sensor [part_number=DS18B20 package="TO92 [THT]"]
  R1 = Resistor [tolerance=±5% resistance=4.7k package=THT]

nets:
  N1: Arduino_Uno_and_Ethernet_shield.D3, T1.DQ, R1.Pin_0
  N2: Arduino_Uno_and_Ethernet_shield.+5V, T1.+Vdd, R1.Pin_1
  GND: Arduino_Uno_and_Ethernet_shield.GND, T1.GND

custom parts:
  DS18B20 Temperature Sensor: A DS18B20 temperature sensor
