# Fritzing sketch LM35 (saved by Fritzing 0.7.7b)

parts:
  Arduino1 = Arduino
  T2 = LM35 Temperature Sensor [package="TO92 [THT]"]

nets:
  N1: Arduino1.aref, Arduino1.3V3
  N2: Arduino1.+5V, T2.+Vs
  GND: Arduino1.GND, T2.GND
  N3: Arduino1.A1, T2.Vout
